// Digital circuit LeTecMat.dig as structural Verilog
module LeTecMat (
  input  clk
);

  wire _1_a, _1_b, _2_b, _3_b, _4_a, _7_a, A_b, E_a, letecmat4x4_1_kp;
  wire [3:0] letecmat4x4_1_q0;

  Switch _1 (.A(_1_a), .B(_1_b));
  Switch _4 (.A(_4_a), .B(_1_b));
  Switch _7 (.A(_7_a), .B(_1_b));
  Switch E (.A(E_a), .B(_1_b));
  Switch _2 (.A(_1_a), .B(_2_b));
  Switch _5 (.A(_4_a), .B(_2_b));
  Switch _8 (.A(_7_a), .B(_2_b));
  Switch _0 (.A(E_a), .B(_2_b));
  PullDown pulldown_1 (.out(_1_b));
  Switch _3 (.A(_1_a), .B(_3_b));
  Switch _6 (.A(_4_a), .B(_3_b));
  Switch _9 (.A(_7_a), .B(_3_b));
  Switch F (.A(E_a), .B(_3_b));
  PullDown pulldown_2 (.out(_2_b));
  Switch A (.A(_1_a), .B(A_b));
  Switch B (.A(_4_a), .B(A_b));
  Switch C (.A(_7_a), .B(A_b));
  Switch D (.A(E_a), .B(A_b));
  PullDown pulldown_3 (.out(_3_b));
  PullDown pulldown_4 (.out(A_b));
  LeTecMat4x4 letecmat4x4_1 (
    .clk(clk), .L0(_1_a), .L1(_4_a), .L2(_7_a), .L3(E_a), .C0(_1_b), .C1(_2_b), .C2(_3_b), .C3(A_b),
    .Q0(letecmat4x4_1_q0[0]), .Q1(letecmat4x4_1_q0[1]), .Q2(letecmat4x4_1_q0[2]), .Q3(letecmat4x4_1_q0[3]),
    .Kp(letecmat4x4_1_kp));
  Seven_Seg_Hex seven_seg_hex_1 (.d(letecmat4x4_1_q0), .dp(letecmat4x4_1_kp));

  // Notes on the sheet:
  //   clk: Hz: 30
endmodule
